// Logisim project control-logic.circ as structural Verilog: 3 circuits, main circuit control_logic
module control_logic (
  input  [31:0] Instruction,
  input  BrEq,
  input  BrLt,
  output PCSel,
  output RegWEn,
  output [2:0] ImmSel,
  output BrUn,
  output ASel,
  output BSel,
  output [3:0] ALUSel,
  output MemRW,
  output [1:0] WBSel
);

  wire and_1_out, and_2_out, and_3_out, and_4_out, and_5_out, and_6_out, comparator_1_eq, comparator_2_eq,
       comparator_3_eq, comparator_4_eq, comparator_5_eq, comparator_6_eq, I_0x5, multi_compare_1_o1,
       multi_compare_1_o2, multi_compare_1_o3, multi_compare_1_o4, multi_compare_1_o5, multi_compare_1_o6,
       multi_compare_1_o7, multi_compare_1_o8, multi_compare_1_o9, multi_compare_1_o10, multi_compare_1_o11,
       multi_compare_1_o12, multi_compare_func3_1_o1, multi_compare_func3_1_o2, multi_compare_func3_1_o3,
       multi_compare_func3_2_o1, multi_compare_func3_2_o2, multi_compare_func3_2_o3,
       multi_compare_func3_2_o4, multi_compare_func3_2_o6, multi_compare_func3_2_o7,
       multi_compare_func3_3_o1, multi_compare_func3_3_o2, multi_compare_func3_3_o4,
       multi_compare_func3_3_o5, multi_compare_func3_3_o6, multi_compare_func3_3_o7,
       multi_compare_func3_4_o1, multi_compare_func3_4_o2, multi_compare_func3_4_o3,
       multi_compare_func3_5_o1, multi_compare_func3_5_o2, multi_compare_func3_5_o4,
       multi_compare_func3_5_o5, multi_compare_func3_5_o6, multi_compare_func3_5_o7, not_1_out, not_2_out,
       not_3_out, not_4_out, not_5_out, or_1_out, or_2_out, r19, r20;
  wire [2:0] undriven;
  wire [5:0] ROM_In;
  wire [15:14] rom_1_data;

  // Probe on Instruction[6:0]
  // Probe on Instruction[31:25]
  // Probe on {Instruction[14:12], Instruction[31:25]}
  // Probe on Instruction[14:12]
  ROM #(.addrWidth(6), .dataWidth(16)) rom_1 (
    .addr(ROM_In), .data({rom_1_data, WBSel, MemRW, ALUSel, BSel, ASel, BrUn, ImmSel, RegWEn}));
  multi_compare_func3 multi_compare_func3_1 (
    .op_constant(7'b0000011), .in_4(3'b000), .in_5(3'b001), .in_6(3'b010), .func3(Instruction[14:12]),
    .opcode(Instruction[6:0]), .O1(multi_compare_func3_1_o1), .O2(multi_compare_func3_1_o2),
    .O3(multi_compare_func3_1_o3));  // open: in_8, in_9, in_10, in_7, O5, O6, O7, O4
  multi_compare_func3 multi_compare_func3_2 (
    .op_constant(7'b0010011), .in_4(3'b000), .in_5(3'b001), .in_6(3'b010), .in_8(3'b101), .in_9(3'b110),
    .in_10(3'b111), .in_7(3'b100), .func3(Instruction[14:12]), .opcode(Instruction[6:0]),
    .O1(multi_compare_func3_2_o1), .O2(multi_compare_func3_2_o2), .O3(multi_compare_func3_2_o3), .O5(I_0x5),
    .O6(multi_compare_func3_2_o6), .O7(multi_compare_func3_2_o7), .O4(multi_compare_func3_2_o4));
  multi_compare_func3 multi_compare_func3_3 (
    .op_constant(7'b1100011), .in_4(3'b000), .in_5(3'b001), .in_6(undriven), .in_8(3'b101), .in_9(3'b110),
    .in_10(3'b111), .in_7(3'b100), .func3(Instruction[14:12]), .opcode(Instruction[6:0]),
    .O1(multi_compare_func3_3_o1), .O2(multi_compare_func3_3_o2), .O5(multi_compare_func3_3_o5),
    .O6(multi_compare_func3_3_o6), .O7(multi_compare_func3_3_o7), .O4(multi_compare_func3_3_o4));  // open: O3
  multi_compare_func3 multi_compare_func3_4 (
    .op_constant(7'b0100011), .in_4(3'b000), .in_5(3'b001), .in_6(3'b010), .func3(Instruction[14:12]),
    .opcode(Instruction[6:0]), .O1(multi_compare_func3_4_o1), .O2(multi_compare_func3_4_o2),
    .O3(multi_compare_func3_4_o3));  // open: in_8, in_9, in_10, in_7, O5, O6, O7, O4
  multi_compare multi_compare_1 (
    .op_constant(7'b0110011), .in_4({10{1'b0}}), .in_5(10'h1), .in_6(10'h20), .in_8(10'h81), .in_9(10'h181),
    .in_7(10'h80), .in_10(10'h100), .in_11(10'h200), .in_12(10'h280), .in_13(10'h2a0), .in_14(10'h300),
    .in_15(10'h380), .func37({Instruction[14:12], Instruction[31:25]}), .opcode(Instruction[6:0]),
    .O1(multi_compare_1_o1), .O2(multi_compare_1_o2), .O3(multi_compare_1_o3), .O5(multi_compare_1_o5),
    .O6(multi_compare_1_o6), .O4(multi_compare_1_o4), .O7(multi_compare_1_o7), .O8(multi_compare_1_o8),
    .O9(multi_compare_1_o9), .O10(multi_compare_1_o10), .O11(multi_compare_1_o11), .O12(multi_compare_1_o12));
  Comparator #(.width(7)) comparator_1 (.a(Instruction[6:0]), .b(7'b0010111), .eq(comparator_1_eq));  // open: gt, lt
  Comparator #(.width(7)) comparator_2 (.a(Instruction[6:0]), .b(7'b0110111), .eq(comparator_2_eq));  // open: gt, lt
  Comparator #(.width(7)) comparator_3 (.a(Instruction[6:0]), .b(7'b1101111), .eq(comparator_3_eq));  // open: gt, lt
  Comparator #(.width(7)) comparator_4 (.a(Instruction[6:0]), .b(7'b1100111), .eq(comparator_4_eq));  // open: gt, lt
  Demultiplexer demultiplexer_1 (.out0(r19), .out1(r20), .in(I_0x5), .sel(Instruction[30]));
  Priority_Encoder #(.select_enc(6)) priority_encoder_1 (
    .in0(multi_compare_1_o1), .in1(multi_compare_1_o2), .in2(multi_compare_1_o3), .in3(multi_compare_1_o4),
    .in4(multi_compare_1_o5), .in5(multi_compare_1_o6), .in6(multi_compare_1_o7), .in7(multi_compare_1_o8),
    .in8(multi_compare_1_o9), .in9(multi_compare_1_o10), .in10(multi_compare_1_o11),
    .in11(multi_compare_1_o12), .in12(multi_compare_func3_1_o1), .in13(multi_compare_func3_1_o2),
    .in14(multi_compare_func3_1_o3), .in15(multi_compare_func3_2_o1), .in16(multi_compare_func3_2_o2),
    .in17(multi_compare_func3_2_o3), .in18(multi_compare_func3_2_o4), .in19(r19), .in20(r20),
    .in21(multi_compare_func3_2_o6), .in22(multi_compare_func3_2_o7), .in23(multi_compare_func3_4_o1),
    .in24(multi_compare_func3_4_o2), .in25(multi_compare_func3_4_o3), .in26(multi_compare_func3_3_o1),
    .in27(multi_compare_func3_3_o2), .in28(multi_compare_func3_3_o4), .in29(multi_compare_func3_3_o5),
    .in30(multi_compare_func3_3_o6), .in31(multi_compare_func3_3_o7), .in32(comparator_1_eq),
    .in33(comparator_2_eq), .in34(comparator_3_eq), .in35(comparator_4_eq), .out(ROM_In));  // open: in36, in37, in38, in39, in40, in41, in42, in43, in44, in45, in46, in47, in48, in49, in50, in51, in52, in53, in54, in55, in56, in57, in58, in59, in60, in61, in62, in63, gs, en_out, en_in
  and and_1 (and_1_out, BrLt, multi_compare_func3_5_o6, BrUn);
  multi_compare_func3 multi_compare_func3_5 (
    .op_constant(7'b1100011), .in_4(3'b000), .in_5(3'b001), .in_8(3'b101), .in_9(3'b110), .in_10(3'b111),
    .in_7(3'b100), .func3(Instruction[14:12]), .opcode(Instruction[6:0]), .O1(multi_compare_func3_5_o1),
    .O2(multi_compare_func3_5_o2), .O5(multi_compare_func3_5_o5), .O6(multi_compare_func3_5_o6),
    .O7(multi_compare_func3_5_o7), .O4(multi_compare_func3_5_o4));  // open: in_6, O3
  and and_2 (and_2_out, BrEq, multi_compare_func3_5_o1);
  not not_1 (not_1_out, BrUn);
  not not_2 (not_2_out, BrLt);
  not not_3 (not_3_out, BrUn);
  and and_3 (and_3_out, multi_compare_func3_5_o2, not_4_out);
  not not_4 (not_4_out, BrEq);
  and and_4 (and_4_out, BrLt, multi_compare_func3_5_o4, not_1_out);
  and and_5 (and_5_out, not_2_out, multi_compare_func3_5_o5, not_3_out);
  not not_5 (not_5_out, BrLt);
  Comparator #(.width(7)) comparator_5 (.a(Instruction[6:0]), .b(7'b1101111), .eq(comparator_5_eq));  // open: gt, lt
  Comparator #(.width(7)) comparator_6 (.a(Instruction[6:0]), .b(7'b1100111), .eq(comparator_6_eq));  // open: gt, lt
  and and_6 (and_6_out, not_5_out, multi_compare_func3_5_o7, BrUn);
  or or_1 (or_1_out, comparator_5_eq, comparator_6_eq);
  or or_2 (or_2_out, and_2_out, and_3_out, and_4_out, and_5_out, and_1_out, and_6_out);
  or or_3 (PCSel, or_1_out, or_2_out);

  // Other names for the same wires on the sheet: func7[6:0] = Instruction[31:25];
  //   func37[9:0] = {Instruction[14:12], Instruction[31:25]}; func3[2:0] = Instruction[14:12];
  //   opcode[6:0] = Instruction[6:0]

  // Notes on the sheet:
  //   INPUTS to your circuit
  //   Connect ROM Input here ->
  //   contents of rom_1 (hex, n*v repeats v):
  //   1001 1401 1601 1081 1481 1581 1101 1201 1281 1681 1301 1381 41 41 41 1041 10c1 1141 1241 12c1 16c1
  //   1341 13c1 842 842 842 4*64 74 74 1067 17e7 2069 2041
  //   ROM FOR CONTROL LOGIC
  //   DON'T CHANGE THE LOCATIONS OF THE INPUTS AND OUTPUTS!
  //   This is only if you choose to do the ROM option
  //   CONNECT
  //   WIRE
  //   TO
  //   USE
  //   ROM
  //   OUTPUT from your circuit
  //   Reminder: If using ROM, use combinational logic for PCSel
endmodule

module multi_compare (
  input  [6:0] opcode,
  input  [6:0] op_constant,
  input  [9:0] func37,
  input  [9:0] in_4,
  input  [9:0] in_5,
  input  [9:0] in_6,
  input  [9:0] in_7,
  input  [9:0] in_8,
  input  [9:0] in_9,
  input  [9:0] in_10,
  input  [9:0] in_11,
  input  [9:0] in_12,
  input  [9:0] in_13,
  input  [9:0] in_14,
  input  [9:0] in_15,
  output O1,
  output O2,
  output O3,
  output O4,
  output O5,
  output O6,
  output O7,
  output O8,
  output O9,
  output O10,
  output O11,
  output O12
);

  wire comparator_1_eq, comparator_2_eq, comparator_3_eq, comparator_4_eq, comparator_5_eq, comparator_6_eq,
       comparator_7_eq, comparator_8_eq, comparator_9_eq, comparator_10_eq, comparator_11_eq,
       comparator_12_eq, comparator_13_eq, comparator_14_eq, comparator_15_eq, comparator_16_eq;

  Comparator #(.width(7)) comparator_1 (.a(opcode), .b(op_constant), .eq(comparator_1_eq));  // open: gt, lt
  Comparator #(.width(10)) comparator_2 (.a(func37), .b(in_4), .eq(comparator_2_eq));  // open: gt, lt
  Comparator #(.width(10)) comparator_3 (.a(func37), .b(in_5), .eq(comparator_3_eq));  // open: gt, lt
  Comparator #(.width(10)) comparator_4 (.a(func37), .b(in_6), .eq(comparator_4_eq));  // open: gt, lt
  Comparator #(.width(7)) comparator_5 (.a(opcode), .b(op_constant), .eq(comparator_5_eq));  // open: gt, lt
  Comparator #(.width(10)) comparator_6 (.a(func37), .b(in_7), .eq(comparator_6_eq));  // open: gt, lt
  Comparator #(.width(10)) comparator_7 (.a(func37), .b(in_8), .eq(comparator_7_eq));  // open: gt, lt
  Comparator #(.width(10)) comparator_8 (.a(func37), .b(in_9), .eq(comparator_8_eq));  // open: gt, lt
  Comparator #(.width(7)) comparator_9 (.a(opcode), .b(op_constant), .eq(comparator_9_eq));  // open: gt, lt
  Comparator #(.width(10)) comparator_10 (.a(func37), .b(in_10), .eq(comparator_10_eq));  // open: gt, lt
  Comparator #(.width(10)) comparator_11 (.a(func37), .b(in_11), .eq(comparator_11_eq));  // open: gt, lt
  Comparator #(.width(10)) comparator_12 (.a(func37), .b(in_12), .eq(comparator_12_eq));  // open: gt, lt
  and and_1 (O1, comparator_2_eq, comparator_1_eq);
  and and_2 (O2, comparator_3_eq, comparator_1_eq);
  and and_3 (O3, comparator_4_eq, comparator_1_eq);
  Comparator #(.width(7)) comparator_13 (.a(opcode), .b(op_constant), .eq(comparator_13_eq));  // open: gt, lt
  Comparator #(.width(10)) comparator_14 (.a(func37), .b(in_13), .eq(comparator_14_eq));  // open: gt, lt
  Comparator #(.width(10)) comparator_15 (.a(func37), .b(in_14), .eq(comparator_15_eq));  // open: gt, lt
  Comparator #(.width(10)) comparator_16 (.a(func37), .b(in_15), .eq(comparator_16_eq));  // open: gt, lt
  and and_4 (O4, comparator_6_eq, comparator_5_eq);
  and and_5 (O5, comparator_7_eq, comparator_5_eq);
  and and_6 (O6, comparator_8_eq, comparator_5_eq);
  and and_7 (O7, comparator_10_eq, comparator_9_eq);
  and and_8 (O8, comparator_11_eq, comparator_9_eq);
  and and_9 (O9, comparator_12_eq, comparator_9_eq);
  and and_10 (O10, comparator_14_eq, comparator_13_eq);
  and and_11 (O11, comparator_15_eq, comparator_13_eq);
  and and_12 (O12, comparator_16_eq, comparator_13_eq);

  // Other names for the same wires on the sheet: I1[9:0] = func37; I1_constant[9:0] = in_4; I2_constant[9:0] = in_5;
  //   I3_constant[9:0] = in_6; I4_constant[9:0] = in_7; I5_constant[9:0] = in_8; I6_constant[9:0] = in_9;
  //   I7_constant[9:0] = in_10; I8_constant[9:0] = in_11; I9_constant[9:0] = in_12; I10_constant[9:0] = in_13;
  //   I11_constant[9:0] = in_14; I12_constant[9:0] = in_15
endmodule

module multi_compare_func3 (
  input  [6:0] opcode,
  input  [6:0] op_constant,
  input  [2:0] func3,
  input  [2:0] in_4,
  input  [2:0] in_5,
  input  [2:0] in_6,
  input  [2:0] in_7,
  input  [2:0] in_8,
  input  [2:0] in_9,
  input  [2:0] in_10,
  output O1,
  output O2,
  output O3,
  output O4,
  output O5,
  output O6,
  output O7
);

  wire comparator_1_eq, comparator_2_eq, comparator_3_eq, comparator_4_eq, comparator_5_eq, comparator_6_eq,
       comparator_7_eq, comparator_8_eq, comparator_9_eq;

  Comparator #(.width(7)) comparator_1 (.a(opcode), .b(op_constant), .eq(comparator_1_eq));  // open: gt, lt
  Comparator #(.width(3)) comparator_2 (.a(func3), .b(in_4), .eq(comparator_2_eq));  // open: gt, lt
  Comparator #(.width(3)) comparator_3 (.a(func3), .b(in_5), .eq(comparator_3_eq));  // open: gt, lt
  Comparator #(.width(3)) comparator_4 (.a(func3), .b(in_6), .eq(comparator_4_eq));  // open: gt, lt
  Comparator #(.width(7)) comparator_5 (.a(opcode), .b(op_constant), .eq(comparator_5_eq));  // open: gt, lt
  Comparator #(.width(3)) comparator_6 (.a(func3), .b(in_7), .eq(comparator_6_eq));  // open: gt, lt
  Comparator #(.width(3)) comparator_7 (.a(func3), .b(in_8), .eq(comparator_7_eq));  // open: gt, lt
  Comparator #(.width(3)) comparator_8 (.a(func3), .b(in_9), .eq(comparator_8_eq));  // open: gt, lt
  Comparator #(.width(3)) comparator_9 (.a(func3), .b(in_10), .eq(comparator_9_eq));  // open: gt, lt
  and and_1 (O1, comparator_2_eq, comparator_1_eq);
  and and_2 (O2, comparator_3_eq, comparator_1_eq);
  and and_3 (O3, comparator_4_eq, comparator_1_eq);
  and and_4 (O4, comparator_6_eq, comparator_5_eq);
  and and_5 (O5, comparator_7_eq, comparator_5_eq);
  and and_6 (O6, comparator_8_eq, comparator_5_eq);
  and and_7 (O7, comparator_9_eq, comparator_5_eq);

  // Other names for the same wires on the sheet: I1[2:0] = func3; I1_constant[2:0] = in_4; I2_constant[2:0] = in_5;
  //   I3_constant[2:0] = in_6; I4_constant[2:0] = in_7; I5_constant[2:0] = in_8; I6_constant[2:0] = in_9;
  //   I7_constant[2:0] = in_10
endmodule
