// Logisim project imm-gen.circ as structural Verilog: 1 circuit, main circuit imm_gen
module imm_gen (
  input  [31:0] Instruction,
  input  [2:0] ImmSel,
  output [31:0] Immediate
);

  wire [31:0] BImm, bit_extender_3_out, SImm;
  wire [31:20] JImm;

  assign SImm = {{20{Instruction[31]}}, {Instruction[31:25], Instruction[11:7]}};  // Bit_Extender bit_extender_1
  assign BImm = {{19{Instruction[31]}}, {Instruction[31], Instruction[7], Instruction[30:25], Instruction[11:8], 1'b0}};  // Bit_Extender bit_extender_2
  // Probe on Instruction[31:20]
  assign bit_extender_3_out = {{20{Instruction[31]}}, Instruction[31:20]};  // Bit_Extender bit_extender_3
  // Probe on bit_extender_3_out
  Multiplexer #(.select(3), .width(32)) multiplexer_1 (
    .in0(bit_extender_3_out), .in1(SImm), .in2(BImm), .in3({Instruction[31:12], {12{1'b0}}}),
    .in4({JImm, Instruction[19:12], Instruction[20], Instruction[30:21], 1'b0}), .out(Immediate), .sel(ImmSel));  // open: in5, in6, in7
  assign JImm = {{11{Instruction[31]}}, Instruction[31]};  // Bit_Extender bit_extender_4

  // Other names for the same wires on the sheet: JImm[19:1] = {Instruction[19:12], Instruction[20], Instruction[30:21]};
  //   UImm[31:12] = Instruction[31:12]

  // Notes on the sheet:
  //   INPUTS to your circuit
  //   DON'T CHANGE THE LOCATIONS OF THE INPUTS AND OUTPUTS!
  //   OUTPUT from your circuit
endmodule
