// Logisim project partial-load.circ as structural Verilog: 1 circuit, main circuit partial_load
module partial_load (
  input  [31:0] Instruction,
  input  [31:0] MemAddress,
  input  [31:0] DataFromMem,
  output [31:0] DataToReg
);

  wire and_1_out, and_2_out, and_3_out, and_4_out, and_5_out, and_6_out, and_7_out, and_15_out,
       comparator_1_eq, comparator_2_eq, comparator_3_eq, comparator_4_eq, comparator_5_eq, comparator_6_eq,
       comparator_7_eq, comparator_8_eq, comparator_9_eq, comparator_10_eq, comparator_11_eq;
  wire [31:0] and_10_out, bit_extender_1_out, bit_extender_2_out, bit_extender_3_out, bit_extender_4_out,
       bit_extender_5_out, bit_extender_6_out, bit_extender_7_out, bit_extender_8_out, bit_extender_9_out,
       bit_extender_10_out, bit_extender_11_out, bit_extender_12_out, bit_extender_13_out,
       bit_extender_14_out, bit_extender_15_out, bit_extender_16_out, bit_extender_17_out,
       bit_extender_18_out, bit_extender_19_out, bit_extender_20_out, bit_extender_21_out,
       bit_extender_22_out;

  Comparator #(.width(7)) comparator_1 (.a(Instruction[6:0]), .b(7'b0000011), .eq(comparator_1_eq));  // open: gt, lt
  Comparator #(.width(7)) comparator_2 (.a(Instruction[6:0]), .b(7'b0000011), .eq(comparator_2_eq));  // open: gt, lt
  Comparator #(.width(5)) comparator_3 (
    .a({MemAddress[1:0], Instruction[14:12]}), .b({5{1'b0}}), .eq(comparator_3_eq));  // open: gt, lt
  Comparator #(.width(5)) comparator_4 (
    .a({MemAddress[1:0], Instruction[14:12]}), .b(5'b00001), .eq(comparator_4_eq));  // open: gt, lt
  Comparator #(.width(5)) comparator_5 (
    .a({MemAddress[1:0], Instruction[14:12]}), .b(5'b01001), .eq(comparator_5_eq));  // open: gt, lt
  Comparator #(.width(5)) comparator_6 (
    .a({MemAddress[1:0], Instruction[14:12]}), .b(5'b10001), .eq(comparator_6_eq));  // open: gt, lt
  Comparator #(.width(5)) comparator_7 (
    .a({MemAddress[1:0], Instruction[14:12]}), .b(5'b01000), .eq(comparator_7_eq));  // open: gt, lt
  Comparator #(.width(5)) comparator_8 (
    .a({MemAddress[1:0], Instruction[14:12]}), .b({5{1'b0}}), .eq(comparator_8_eq));  // open: gt, lt
  Comparator #(.width(5)) comparator_9 (
    .a({MemAddress[1:0], Instruction[14:12]}), .b(5'b11000), .eq(comparator_9_eq));  // open: gt, lt
  and and_1 (and_1_out, comparator_1_eq, comparator_4_eq);
  assign bit_extender_1_out = {{16{DataFromMem[15]}}, DataFromMem[15:0]};  // Bit_Extender bit_extender_1
  and and_2 (and_2_out, comparator_1_eq, comparator_5_eq);
  assign bit_extender_2_out = {{16{DataFromMem[23]}}, DataFromMem[23:8]};  // Bit_Extender bit_extender_2
  and and_3 (and_3_out, comparator_1_eq, comparator_6_eq);
  assign bit_extender_3_out = {{16{DataFromMem[31]}}, DataFromMem[31:16]};  // Bit_Extender bit_extender_3
  assign bit_extender_4_out = {{31{and_4_out}}, and_4_out};  // Bit_Extender bit_extender_4
  and and_4 (and_4_out, comparator_2_eq, comparator_3_eq);
  assign bit_extender_5_out = {{24{DataFromMem[7]}}, DataFromMem[7:0]};  // Bit_Extender bit_extender_5
  assign bit_extender_6_out = {{31{and_5_out}}, and_5_out};  // Bit_Extender bit_extender_6
  and and_5 (and_5_out, comparator_2_eq, comparator_7_eq);
  assign bit_extender_7_out = {{24{DataFromMem[15]}}, DataFromMem[15:8]};  // Bit_Extender bit_extender_7
  assign bit_extender_8_out = {{31{and_6_out}}, and_6_out};  // Bit_Extender bit_extender_8
  and and_6 (and_6_out, comparator_2_eq, comparator_8_eq);
  assign bit_extender_9_out = {{24{DataFromMem[23]}}, DataFromMem[23:16]};  // Bit_Extender bit_extender_9
  and and_7 (and_7_out, comparator_2_eq, comparator_9_eq);
  assign bit_extender_10_out = {{24{DataFromMem[31]}}, DataFromMem[31:24]};  // Bit_Extender bit_extender_10
  assign bit_extender_11_out = {{31{and_1_out}}, and_1_out};  // Bit_Extender bit_extender_11
  assign bit_extender_12_out = {{31{and_2_out}}, and_2_out};  // Bit_Extender bit_extender_12
  // AND_Gate and_8 has open pins: in0=bit_extender_12_out, in1=bit_extender_2_out, out=open
  assign bit_extender_13_out = {{31{and_3_out}}, and_3_out};  // Bit_Extender bit_extender_13
  // AND_Gate and_9 has open pins: in0=bit_extender_13_out, in1=bit_extender_3_out, out=open
  assign and_10_out = bit_extender_4_out & bit_extender_5_out;  // AND_Gate and_10, 32 bits wide
  // AND_Gate and_11 has open pins: in0=bit_extender_6_out, in1=bit_extender_7_out, out=open
  // AND_Gate and_12 has open pins: in0=bit_extender_8_out, in1=bit_extender_9_out, out=open
  assign bit_extender_14_out = {{31{and_7_out}}, and_7_out};  // Bit_Extender bit_extender_14
  // AND_Gate and_13 has open pins: in0=bit_extender_14_out, in1=bit_extender_10_out, out=open
  // AND_Gate and_14 has open pins: in0=bit_extender_11_out, in1=bit_extender_1_out, out=open
  assign bit_extender_15_out = {{16{DataFromMem[15]}}, DataFromMem[15:0]};  // Bit_Extender bit_extender_15
  assign bit_extender_16_out = {{24{DataFromMem[23]}}, DataFromMem[23:16]};  // Bit_Extender bit_extender_16
  assign bit_extender_17_out = {{24{DataFromMem[31]}}, DataFromMem[31:24]};  // Bit_Extender bit_extender_17
  Comparator #(.width(7)) comparator_10 (.a(Instruction[6:0]), .b(7'b0000011), .eq(comparator_10_eq));  // open: gt, lt
  Comparator #(.width(5)) comparator_11 (
    .a({MemAddress[1:0], Instruction[14:12]}), .b(5'b00010), .eq(comparator_11_eq));  // open: gt, lt
  assign bit_extender_18_out = {{24{DataFromMem[7]}}, DataFromMem[7:0]};  // Bit_Extender bit_extender_18
  assign bit_extender_19_out = {{24{DataFromMem[15]}}, DataFromMem[15:8]};  // Bit_Extender bit_extender_19
  assign bit_extender_20_out = {{16{DataFromMem[31]}}, DataFromMem[31:16]};  // Bit_Extender bit_extender_20
  // Probe on Instruction[14:12]
  // Probe on MemAddress[1:0]
  Multiplexer #(.select(5), .width(32)) multiplexer_1 (
    .in0(bit_extender_18_out), .in1(bit_extender_15_out), .in2(DataFromMem), .in8(bit_extender_19_out),
    .in9(bit_extender_22_out), .in16(bit_extender_16_out), .in17(bit_extender_20_out),
    .in24(bit_extender_17_out), .out(DataToReg), .sel({MemAddress[1:0], Instruction[14:12]}));  // open: in3, in4, in5, in6, in7, in10, in11, in12, in13, in14, in15, in18, in19, in20, in21, in22, in23, in25, in26, in27, in28, in29, in30, in31
  // Probe on DataToReg
  // Probe on {MemAddress[1:0], Instruction[14:12]}
  assign bit_extender_21_out = {{31{and_15_out}}, and_15_out};  // Bit_Extender bit_extender_21
  and and_15 (and_15_out, comparator_10_eq, comparator_11_eq);
  // AND_Gate and_16 has open pins: in0=bit_extender_21_out, in1=DataFromMem, out=open
  assign bit_extender_22_out = {{16{DataFromMem[23]}}, DataFromMem[23:8]};  // Bit_Extender bit_extender_22

  // Other names for the same wires on the sheet: data0[7:0] = DataFromMem[7:0]; data3[7:0] = DataFromMem[31:24];
  //   func3[2:0] = Instruction[14:12]; MemAdd[1:0] = MemAddress[1:0]; data1[7:0] = DataFromMem[15:8];
  //   data2[7:0] = DataFromMem[23:16]; opcode[6:0] = Instruction[6:0]

  // Notes on the sheet:
  //   INPUTS to your circuit
  //   DON'T CHANGE THE LOCATIONS OF THE INPUTS AND OUTPUTS!
  //   OUTPUT from your circuit
endmodule
