// Logisim project partial-store.circ as structural Verilog: 1 circuit, main circuit partial_store
module partial_store (
  input  [31:0] Instruction,
  input  [31:0] MemAddress,
  input  [31:0] DataFromReg,
  input  MemRW,
  output [3:0] MemWriteMask,
  output [31:0] DataToMem
);

  wire comparator_1_eq;
  wire [1:0] not_1_out;
  wire [3:0] bit_extender_1_out, decoder_1_out0, multiplexer_5_out;

  Multiplexer #(.select(5), .width(8)) multiplexer_1 (
    .in0(DataFromReg[7:0]), .in1(DataFromReg[7:0]), .in2(DataFromReg[7:0]), .in3({8{1'b0}}), .in4({8{1'b0}}),
    .in5({8{1'b0}}), .in6({8{1'b0}}), .in7({8{1'b0}}), .in8({8{1'b0}}), .in9({8{1'b0}}), .in10({8{1'b0}}),
    .in11({8{1'b0}}), .in12({8{1'b0}}), .in13({8{1'b0}}), .in14({8{1'b0}}), .in15({8{1'b0}}),
    .in16({8{1'b0}}), .in17({8{1'b0}}), .in18({8{1'b0}}), .in19({8{1'b0}}), .in20({8{1'b0}}),
    .in21({8{1'b0}}), .in22({8{1'b0}}), .in23({8{1'b0}}), .in24({8{1'b0}}), .in25({8{1'b0}}),
    .in26({8{1'b0}}), .in27({8{1'b0}}), .in28({8{1'b0}}), .in29({8{1'b0}}), .in30({8{1'b0}}),
    .in31({8{1'b0}}), .out(DataToMem[7:0]), .sel({MemAddress[1:0], Instruction[14:12]}));
  Multiplexer #(.select(5), .width(8)) multiplexer_2 (
    .in0({8{1'b0}}), .in1(DataFromReg[15:8]), .in2(DataFromReg[15:8]), .in3({8{1'b0}}), .in4({8{1'b0}}),
    .in5({8{1'b0}}), .in6({8{1'b0}}), .in7({8{1'b0}}), .in8(DataFromReg[7:0]), .in9({8{1'b0}}),
    .in10({8{1'b0}}), .in11({8{1'b0}}), .in12({8{1'b0}}), .in13({8{1'b0}}), .in14({8{1'b0}}),
    .in15({8{1'b0}}), .in16({8{1'b0}}), .in17({8{1'b0}}), .in18({8{1'b0}}), .in19({8{1'b0}}),
    .in20({8{1'b0}}), .in21({8{1'b0}}), .in22({8{1'b0}}), .in23({8{1'b0}}), .in24({8{1'b0}}),
    .in25({8{1'b0}}), .in26({8{1'b0}}), .in27({8{1'b0}}), .in28({8{1'b0}}), .in29({8{1'b0}}),
    .in30({8{1'b0}}), .in31({8{1'b0}}), .out(DataToMem[15:8]), .sel({MemAddress[1:0], Instruction[14:12]}));
  Multiplexer #(.select(5), .width(8)) multiplexer_3 (
    .in0({8{1'b0}}), .in1({8{1'b0}}), .in2(DataFromReg[23:16]), .in3({8{1'b0}}), .in4({8{1'b0}}),
    .in5({8{1'b0}}), .in6({8{1'b0}}), .in7({8{1'b0}}), .in8({8{1'b0}}), .in9({8{1'b0}}), .in10({8{1'b0}}),
    .in11({8{1'b0}}), .in12({8{1'b0}}), .in13({8{1'b0}}), .in14({8{1'b0}}), .in15({8{1'b0}}),
    .in16(DataFromReg[7:0]), .in17(DataFromReg[7:0]), .in18({8{1'b0}}), .in19({8{1'b0}}), .in20({8{1'b0}}),
    .in21({8{1'b0}}), .in22({8{1'b0}}), .in23({8{1'b0}}), .in24({8{1'b0}}), .in25({8{1'b0}}),
    .in26({8{1'b0}}), .in27({8{1'b0}}), .in28({8{1'b0}}), .in29({8{1'b0}}), .in30({8{1'b0}}),
    .in31({8{1'b0}}), .out(DataToMem[23:16]), .sel({MemAddress[1:0], Instruction[14:12]}));
  Multiplexer #(.select(5), .width(8)) multiplexer_4 (
    .in0({8{1'b0}}), .in1({8{1'b0}}), .in2(DataFromReg[31:24]), .in3({8{1'b0}}), .in4({8{1'b0}}),
    .in5({8{1'b0}}), .in6({8{1'b0}}), .in7({8{1'b0}}), .in8({8{1'b0}}), .in9({8{1'b0}}), .in10({8{1'b0}}),
    .in11({8{1'b0}}), .in12({8{1'b0}}), .in13({8{1'b0}}), .in14({8{1'b0}}), .in15({8{1'b0}}),
    .in16({8{1'b0}}), .in17(DataFromReg[15:8]), .in18({8{1'b0}}), .in19({8{1'b0}}), .in20({8{1'b0}}),
    .in21({8{1'b0}}), .in22({8{1'b0}}), .in23({8{1'b0}}), .in24(DataFromReg[7:0]), .in25({8{1'b0}}),
    .in26({8{1'b0}}), .in27({8{1'b0}}), .in28({8{1'b0}}), .in29({8{1'b0}}), .in30({8{1'b0}}),
    .in31({8{1'b0}}), .out(DataToMem[31:24]), .sel({MemAddress[1:0], Instruction[14:12]}));
  Comparator #(.width(3)) comparator_1 (.a(Instruction[14:12]), .b(3'b000), .eq(comparator_1_eq));  // open: gt, lt
  Decoder #(.select(2)) decoder_1 (
    .out0(decoder_1_out0[0]), .out1(decoder_1_out0[1]), .out2(decoder_1_out0[2]), .out3(decoder_1_out0[3]),
    .sel(MemAddress[1:0]), .en(comparator_1_eq));
  not not_1 (not_1_out[0], MemAddress[1]);
  not not_2 (not_1_out[1], MemAddress[1]);
  Multiplexer #(.select(3), .width(4)) multiplexer_5 (
    .in0(decoder_1_out0), .in1({{2{MemAddress[1]}}, not_1_out}), .in2(4'b1111), .out(multiplexer_5_out),
    .sel(Instruction[14:12]));  // open: in3, in4, in5, in6, in7
  assign bit_extender_1_out = {{3{MemRW}}, MemRW};  // Bit_Extender bit_extender_1
  assign MemWriteMask = multiplexer_5_out & bit_extender_1_out;  // AND_Gate and_1, 4 bits wide

  // Other names for the same wires on the sheet: MemAdd[1:0] = MemAddress[1:0];
  //   Sel[4:0] = {MemAddress[1:0], Instruction[14:12]}; data0[7:0] = DataFromReg[7:0]; data1[7:0] = DataFromReg[15:8];
  //   data2[7:0] = DataFromReg[23:16]; data3[7:0] = DataFromReg[31:24]; Mem0[7:0] = DataToMem[7:0];
  //   Mem1[7:0] = DataToMem[15:8]; Mem2[7:0] = DataToMem[23:16]; Mem3[7:0] = DataToMem[31:24];
  //   opcode[6:0] = Instruction[6:0]; func3[2:0] = Instruction[14:12]

  // Notes on the sheet:
  //   INPUTS to your circuit
  //   DON'T CHANGE THE LOCATIONS OF THE INPUTS AND OUTPUTS!
  //   OUTPUT from your circuit
endmodule
