// Logisim project regfile.circ as structural Verilog: 1 circuit, main circuit regfile
module regfile (
  input  [4:0] ReadIndex1,
  input  [4:0] ReadIndex2,
  input  [4:0] WriteIndex,
  input  [31:0] WriteData,
  input  RegWEn,
  input  clk,
  output [31:0] ra,
  output [31:0] sp,
  output [31:0] t0,
  output [31:0] t1,
  output [31:0] t2,
  output [31:0] s0,
  output [31:0] s1,
  output [31:0] a0,
  output [31:0] ReadData1,
  output [31:0] ReadData2
);

  wire E1, E2, E3, E4, E5, E6, E7, E8, E9, E10, E11, E12, E13, E14, E15, E16, E17, E18, E19, E20, E21, E22,
       E23, E24, E25, E26, E27, E28, E29, E30, E31;
  wire [31:0] x3, x4, x11, x12, x13, x14, x15, x16, x17, x18, x19, x20, x21, x22, x23, x24, x25, x26, x27,
       x28, x29, x30, x31;

  Register #(.width(32)) register_1 (.D(WriteData), .en(E1), .clk(clk), .Q(ra), .clr(1'b0));
  Register #(.width(32)) register_2 (.D(WriteData), .en(E2), .clk(clk), .Q(sp), .clr(1'b0));
  Register #(.width(32)) register_3 (.D(WriteData), .en(E3), .clk(clk), .Q(x3), .clr(1'b0));
  Register #(.width(32)) register_4 (.D(WriteData), .en(E4), .clk(clk), .Q(x4), .clr(1'b0));
  Register #(.width(32)) register_5 (.D(WriteData), .en(E5), .clk(clk), .Q(t0), .clr(1'b0));
  Register #(.width(32)) register_6 (.D(WriteData), .en(E6), .clk(clk), .Q(t1), .clr(1'b0));
  Register #(.width(32)) register_7 (.D(WriteData), .en(E7), .clk(clk), .Q(t2), .clr(1'b0));
  Register #(.width(32)) register_8 (.D(WriteData), .en(E8), .clk(clk), .Q(s0), .clr(1'b0));
  Multiplexer #(.select(5), .width(32)) multiplexer_1 (
    .in0({32{1'b0}}), .in1(ra), .in2(sp), .in3(x3), .in4(x4), .in5(t0), .in6(t1), .in7(t2), .in8(s0),
    .in9(s1), .in10(a0), .in11(x11), .in12(x12), .in13(x13), .in14(x14), .in15(x15), .in16(x16), .in17(x17),
    .in18(x18), .in19(x19), .in20(x20), .in21(x21), .in22(x22), .in23(x23), .in24(x24), .in25(x25),
    .in26(x26), .in27(x27), .in28(x28), .in29(x29), .in30(x30), .in31(x31), .out(ReadData1), .sel(ReadIndex1));
  Multiplexer #(.select(5), .width(32)) multiplexer_2 (
    .in0({32{1'b0}}), .in1(ra), .in2(sp), .in3(x3), .in4(x4), .in5(t0), .in6(t1), .in7(t2), .in8(s0),
    .in9(s1), .in10(a0), .in11(x11), .in12(x12), .in13(x13), .in14(x14), .in15(x15), .in16(x16), .in17(x17),
    .in18(x18), .in19(x19), .in20(x20), .in21(x21), .in22(x22), .in23(x23), .in24(x24), .in25(x25),
    .in26(x26), .in27(x27), .in28(x28), .in29(x29), .in30(x30), .in31(x31), .out(ReadData2), .sel(ReadIndex2));
  Demultiplexer #(.select(5)) demultiplexer_1 (
    .out1(E1), .out2(E2), .out3(E3), .out4(E4), .out5(E5), .out6(E6), .out7(E7), .out8(E8), .out9(E9),
    .out10(E10), .out11(E11), .out12(E12), .out13(E13), .out14(E14), .out15(E15), .out16(E16), .out17(E17),
    .out18(E18), .out19(E19), .out20(E20), .out21(E21), .out22(E22), .out23(E23), .out24(E24), .out25(E25),
    .out26(E26), .out27(E27), .out28(E28), .out29(E29), .out30(E30), .out31(E31), .in(RegWEn),
    .sel(WriteIndex));  // open: out0
  Register #(.width(32)) register_9 (.D(WriteData), .en(E9), .clk(clk), .Q(s1), .clr(1'b0));
  Register #(.width(32)) register_10 (.D(WriteData), .en(E10), .clk(clk), .Q(a0), .clr(1'b0));
  Register #(.width(32)) register_11 (.D(WriteData), .en(E11), .clk(clk), .Q(x11), .clr(1'b0));
  Register #(.width(32)) register_12 (.D(WriteData), .en(E12), .clk(clk), .Q(x12), .clr(1'b0));
  Register #(.width(32)) register_13 (.D(WriteData), .en(E13), .clk(clk), .Q(x13), .clr(1'b0));
  Register #(.width(32)) register_14 (.D(WriteData), .en(E14), .clk(clk), .Q(x14), .clr(1'b0));
  Register #(.width(32)) register_15 (.D(WriteData), .en(E15), .clk(clk), .Q(x15), .clr(1'b0));
  Register #(.width(32)) register_16 (.D(WriteData), .en(E16), .clk(clk), .Q(x16), .clr(1'b0));
  Register #(.width(32)) register_17 (.D(WriteData), .en(E17), .clk(clk), .Q(x17), .clr(1'b0));
  Register #(.width(32)) register_18 (.D(WriteData), .en(E18), .clk(clk), .Q(x18), .clr(1'b0));
  Register #(.width(32)) register_19 (.D(WriteData), .en(E19), .clk(clk), .Q(x19), .clr(1'b0));
  Register #(.width(32)) register_20 (.D(WriteData), .en(E20), .clk(clk), .Q(x20), .clr(1'b0));
  Register #(.width(32)) register_21 (.D(WriteData), .en(E21), .clk(clk), .Q(x21), .clr(1'b0));
  Register #(.width(32)) register_22 (.D(WriteData), .en(E22), .clk(clk), .Q(x22), .clr(1'b0));
  Register #(.width(32)) register_23 (.D(WriteData), .en(E23), .clk(clk), .Q(x23), .clr(1'b0));
  Register #(.width(32)) register_24 (.D(WriteData), .en(E24), .clk(clk), .Q(x24), .clr(1'b0));
  Register #(.width(32)) register_25 (.D(WriteData), .en(E25), .clk(clk), .Q(x25), .clr(1'b0));
  Register #(.width(32)) register_26 (.D(WriteData), .en(E26), .clk(clk), .Q(x26), .clr(1'b0));
  Register #(.width(32)) register_27 (.D(WriteData), .en(E27), .clk(clk), .Q(x27), .clr(1'b0));
  Register #(.width(32)) register_28 (.D(WriteData), .en(E28), .clk(clk), .Q(x28), .clr(1'b0));
  Register #(.width(32)) register_29 (.D(WriteData), .en(E29), .clk(clk), .Q(x29), .clr(1'b0));
  Register #(.width(32)) register_30 (.D(WriteData), .en(E30), .clk(clk), .Q(x30), .clr(1'b0));
  Register #(.width(32)) register_31 (.D(WriteData), .en(E31), .clk(clk), .Q(x31), .clr(1'b0));

  // Notes on the sheet:
  //   INPUTS to your circuit
  //   DON'T CHANGE THE LOCATIONS OF THE INPUTS AND OUTPUTS!
  //   These are DEBUG/TEST outputs from your circuit.
  //   OUTPUTS from your circuit
endmodule
